# Fritzing sketch non-contact-voltage-sensor (saved by Fritzing 0.9.2b)
circuit board: 8.46667cm x 5.64444cm
breadboards: 1
perfboards: 1

parts:
  S1 = Momentary Switch [package=ksa_sealed_tac_switch]
  LED1 = smd LED [color="Red (633nm)" package="1206 [SMD]"]
  R1 = Resistor [tolerance=±5% resistance=220 package="0402 [SMD]"]
  R2 = Resistor [tolerance=±5% resistance=100k package="0402 [SMD]"]
  R3 = Resistor [tolerance=±5% resistance=1M package="0402 [SMD]"]
  VCC1 = Battery block 9V
  Q3 = NPN-Transistor [package="TO92 [THT]"]
  Q2 = NPN-Transistor [package="TO92 [THT]"]
  Q1 = NPN-Transistor [package="TO92 [THT]"]

nets (from the schematic view):
  N1: S1.1, VCC1.+
  N2: S1.3, LED1.anode, R2.Pin_0, R3.Pin_0
  N3: LED1.cathode, R1.Pin_0
  N4: R1.Pin_1, Q1.C
  N5: R2.Pin_1, Q2.C
  N6: R3.Pin_1, Q3.C
  N7: VCC1.-, Q1.E
  N8: Q3.E, Q2.B
  N9: Q2.E, Q1.B

notes:
  Material que sirva como antena: pedaço de fio, pedaço de placa de silicio.
